// Logisim project 2_dec novo.circ as structural Verilog: 1 circuit, main circuit 2_dec
// DEC
module _2_dec (
  input  [3:0] INPUT,
  output FETCH_BUSCA,
  output LOAD_LEITURA,
  output ADD_SOMA,
  output \COMP_COMPARAÇÃO ,
  output STORE_ESCRITA,
  output \NOP_SEM_OPERAÇÃO ,
  output \HALT_TÉRMINO ,
  output Sub,
  output Mult,
  output \Divisão 
);

  and and_1 (FETCH_BUSCA, ~INPUT[3], ~INPUT[2], ~INPUT[1], ~INPUT[0]);  // AND_Gate
  and and_2 (LOAD_LEITURA, ~INPUT[3], ~INPUT[2], ~INPUT[1], INPUT[0]);  // AND_Gate
  and and_3 (ADD_SOMA, ~INPUT[3], ~INPUT[2], INPUT[1], ~INPUT[0]);  // AND_Gate
  and and_4 (\COMP_COMPARAÇÃO , ~INPUT[3], INPUT[2], ~INPUT[1], ~INPUT[0]);  // AND_Gate
  and and_5 (STORE_ESCRITA, ~INPUT[3], ~INPUT[2], INPUT[1], INPUT[0]);  // AND_Gate
  and and_6 (\NOP_SEM_OPERAÇÃO , INPUT[3], INPUT[2], INPUT[1], INPUT[0]);
  and and_7 (\HALT_TÉRMINO , ~INPUT[3], INPUT[2], ~INPUT[1], INPUT[0]);  // AND_Gate
  and and_8 (Sub, ~INPUT[3], INPUT[2], INPUT[1], INPUT[0]);  // AND_Gate
  and and_9 (Mult, INPUT[3], INPUT[2], ~INPUT[1], ~INPUT[0]);  // AND_Gate
  and and_10 (\Divisão , INPUT[3], INPUT[2], ~INPUT[1], INPUT[0]);  // AND_Gate

  // Notes on the sheet:
  //   DECODIFICADOR DE INSTRUÇÕES - DEC
endmodule
