// Logisim project 3_acc.circ as structural Verilog: 1 circuit, main circuit 3_acc
// ACC
module _3_acc (
  input  [11:0] IN,
  input  ACC_TG,
  input  ACC_CLEAR,
  output [11:0] ACC_OUT
);

  Register #(.width(12)) ACC (.D(IN), .Q(ACC_OUT), .clk(ACC_TG), .clr(ACC_CLEAR));  // open: en

  // Notes on the sheet:
  //   ACUMULADOR - ACC
endmodule
