// Logisim project 5_ula.circ as structural Verilog: 1 circuit, main circuit 5_ula
// ULA
module _5_ula (
  input  Reset_TG,
  input  [11:0] ACC_IN,
  input  ADD_TG,
  input  [11:0] INPUT,
  input  COMP_TG,
  input  ULA_TG,
  input  [4:0] OPERACAO,
  input  SUB,
  input  DIV,
  input  MULT,
  output [11:0] ACC_OUT,
  output A_MAIOR_B,
  output IGUAIS,
  output B_MAIOR_A
);

  wire and_1_out, not_1_out;
  wire [11:0] ADD_q, adder_1_out, COMP_q, demultiplexer_1_out1, demultiplexer_1_out2, demultiplexer_1_out4,
       demultiplexer_1_out8, demultiplexer_1_out16, Div_q, divider_1_out, MULT_q, multiplier_1_out, Sub_q,
       subtractor_1_out;

  Demultiplexer #(.select(5), .width(12)) demultiplexer_1 (
    .out1(demultiplexer_1_out1), .out2(demultiplexer_1_out2), .out4(demultiplexer_1_out4),
    .out8(demultiplexer_1_out8), .out16(demultiplexer_1_out16), .in(INPUT), .sel(OPERACAO), .en(ULA_TG));  // open: out0, out3, out5, out6, out7, out9, out10, out11, out12, out13, out14, out15, out17, out18, out19, out20, out21, out22, out23, out24, out25, out26, out27, out28, out29, out30, out31
  not not_1 (not_1_out, OPERACAO[1]);
  and and_1 (and_1_out, ~OPERACAO[4], OPERACAO[3], ~OPERACAO[2], not_1_out, ~OPERACAO[0], COMP_TG);  // AND_Gate
  Subtractor #(.width(12)) subtractor_1 (
    .a(ACC_IN), .b(demultiplexer_1_out1), .out(subtractor_1_out));  // open: bin, bout
  Divider #(.width(12)) divider_1 (.a(ACC_IN), .b(demultiplexer_1_out16), .out(divider_1_out));  // open: upper, rem
  Multiplier #(.width(12)) multiplier_1 (
    .a(demultiplexer_1_out2), .b(ACC_IN), .out(multiplier_1_out));  // open: cin, cout
  Adder #(.width(12)) adder_1 (.a(ACC_IN), .b(demultiplexer_1_out4), .out(adder_1_out));  // open: cin, cout
  Register #(.width(12)) ADD (.D(adder_1_out), .Q(ADD_q), .clk(ADD_TG), .clr(Reset_TG));  // open: en
  Register #(.width(12)) COMP (.D(demultiplexer_1_out8), .Q(COMP_q), .clk(COMP_TG));  // open: en, clr
  Register #(.width(12)) u_Sub (.D(subtractor_1_out), .Q(Sub_q), .clk(SUB), .clr(Reset_TG));  // open: en
  Register #(.width(12)) u_Div (.D(divider_1_out), .Q(Div_q), .clk(DIV), .clr(Reset_TG));  // open: en
  Register #(.width(12)) u_MULT (.D(multiplier_1_out), .Q(MULT_q), .clk(MULT), .clr(Reset_TG));  // open: en
  _4_comp8b u_4_comp8b_1 (
    .ENABLE(and_1_out), .A7(ACC_IN[7]), .A6(ACC_IN[6]), .A5(ACC_IN[5]), .A4(ACC_IN[4]), .A3(ACC_IN[3]),
    .A2(ACC_IN[2]), .A1(ACC_IN[1]), .A0(ACC_IN[0]), .B7(COMP_q[7]), .B6(COMP_q[6]), .B5(COMP_q[5]),
    .B4(COMP_q[4]), .B3(COMP_q[3]), .B2(COMP_q[2]), .B1(COMP_q[1]), .B0(COMP_q[0]), .\A_É_MAIOR (A_MAIOR_B),
    .IGUAIS(IGUAIS), .\B_É_MAIOR (B_MAIOR_A));
  assign ACC_OUT = ADD_q | Sub_q | Div_q | MULT_q;  // OR_Gate or_1, 12 bits wide

  // Notes on the sheet:
  //   Mult (00010)
  //   SUB (00001)
  //   Div (10000)
  //   SOMA (00100)
  //   COMPARAÇÃO (01000)
  //   ULA - UNIDADE LÓGICA E ARITMÉTICA (SOMA E COMPARAÇÃO)
endmodule
