// Logisim project 6_uc.circ as structural Verilog: 1 circuit, main circuit UC
module UC (
  input  [11:0] INPUT,
  input  clock,
  output [7:0] \ENDEREÇO ,
  output [4:0] OPERACAO,
  output [20:0] out_5
);

  wire and_1_out, and_2_out, and_3_out, and_4_out, and_5_out, and_6_out, and_7_out, and_8_out, and_9_out,
       and_10_out, n2_dec_1_fetch_busca, \n2_dec_1_halt_término , n2_dec_1_load_leitura,
       \n2_dec_1_nop_sem_operação , n2_dec_1_store_escrita;
  wire [7:0] cont_1_p4, cont_2_p4, cont_3_p4, cont_4_p4, cont_5_p4, cont_6_p4, cont_7_p4, cont_8_p4,
       cont_9_p4, cont_10_p4, controlled_buffer_1_out;

  LED FETCH (.in(n2_dec_1_fetch_busca));
  LED LOAD (.in(n2_dec_1_load_leitura));
  LED ADD (.in(OPERACAO[2]));
  LED COMP (.in(OPERACAO[3]));
  LED STORE (.in(n2_dec_1_store_escrita));
  LED NOP (.in(\n2_dec_1_nop_sem_operação ));
  LED HALT (.in(\n2_dec_1_halt_término ));
  LED SUB (.in(OPERACAO[0]));
  LED Mult (.in(OPERACAO[1]));
  LED Div (.in(OPERACAO[4]));
  _2_dec u_2_dec_1 (
    .INPUT(INPUT[11:8]), .FETCH_BUSCA(n2_dec_1_fetch_busca), .LOAD_LEITURA(n2_dec_1_load_leitura),
    .ADD_SOMA(OPERACAO[2]), .\COMP_COMPARAÇÃO (OPERACAO[3]), .STORE_ESCRITA(n2_dec_1_store_escrita),
    .\NOP_SEM_OPERAÇÃO (\n2_dec_1_nop_sem_operação ), .\HALT_TÉRMINO (\n2_dec_1_halt_término ),
    .Sub(OPERACAO[0]), .Mult(OPERACAO[1]), .\Divisão (OPERACAO[4]));
  and and_1 (and_1_out, n2_dec_1_fetch_busca, clock);
  and and_2 (and_2_out, n2_dec_1_load_leitura, clock);
  and and_3 (and_3_out, OPERACAO[2], clock);
  and and_4 (and_4_out, OPERACAO[3], clock);
  and and_5 (and_5_out, n2_dec_1_store_escrita, clock);
  and and_6 (and_6_out, \n2_dec_1_nop_sem_operação , clock);
  and and_7 (and_7_out, \n2_dec_1_halt_término , clock);
  and and_8 (and_8_out, OPERACAO[0], clock);
  and and_9 (and_9_out, clock, OPERACAO[1]);
  and and_10 (and_10_out, clock, OPERACAO[4]);
  assign controlled_buffer_1_out = and_1_out ? cont_1_p4 : 8'bz;  // Controlled_Buffer controlled_buffer_1
  // CONT cont_1: pin names not known; wires that end beside it: {8{1'b0}}, 8'h3, and_1_out, cont_1_p4
  assign controlled_buffer_1_out = and_2_out ? cont_2_p4 : 8'bz;  // Controlled_Buffer controlled_buffer_2
  // CONT cont_2: pin names not known; wires that end beside it: 8'h6, 8'hb, and_2_out, cont_2_p4
  assign controlled_buffer_1_out = and_3_out ? cont_3_p4 : 8'bz;  // Controlled_Buffer controlled_buffer_3
  // CONT cont_3: pin names not known; wires that end beside it: 8'hd, 8'h13, and_3_out, cont_3_p4
  assign controlled_buffer_1_out = and_4_out ? cont_4_p4 : 8'bz;  // Controlled_Buffer controlled_buffer_4
  // CONT cont_4: pin names not known; wires that end beside it: 8'h1e, 8'h23, and_4_out, cont_4_p4
  assign controlled_buffer_1_out = and_5_out ? cont_5_p4 : 8'bz;  // Controlled_Buffer controlled_buffer_5
  // CONT cont_5: pin names not known; wires that end beside it: 8'h15, 8'h1c, and_5_out, cont_5_p4
  assign controlled_buffer_1_out = and_6_out ? cont_6_p4 : 8'bz;  // Controlled_Buffer controlled_buffer_6
  // CONT cont_6: pin names not known; wires that end beside it: 8'h3e, 8'h3f, and_6_out, cont_6_p4
  assign controlled_buffer_1_out = and_7_out ? cont_7_p4 : 8'bz;  // Controlled_Buffer controlled_buffer_7
  // CONT cont_7: pin names not known; wires that end beside it: 8'h41, 8'h41, and_7_out, cont_7_p4
  assign controlled_buffer_1_out = and_8_out ? cont_8_p4 : 8'bz;  // Controlled_Buffer controlled_buffer_8
  // CONT cont_8: pin names not known; wires that end beside it: 8'h25, 8'h2b, and_8_out, cont_8_p4
  assign controlled_buffer_1_out = and_9_out ? cont_9_p4 : 8'bz;  // Controlled_Buffer controlled_buffer_9
  // CONT cont_9: pin names not known; wires that end beside it: 8'h2d, 8'h33, and_9_out, cont_9_p4
  assign controlled_buffer_1_out = and_10_out ? cont_10_p4 : 8'bz;  // Controlled_Buffer controlled_buffer_10
  // CONT cont_10: pin names not known; wires that end beside it: 8'h35, 8'h3b, and_10_out, cont_10_p4
  ROM #(.dataWidth(21)) rom_1 (.addr(controlled_buffer_1_out), .data(out_5));  // open: sel

  assign \ENDEREÇO  = INPUT[7:0];

  // Notes on the sheet:
  //   mínimo ->
  //   máximo ->
  //   UNIDADE DE CONTROLE
  //   MICROPROGRAMA EM MEMÓRIA ROM
  //   Intervalos em hexadecimal
  //   -> vai para a ULA
  //   MEMÓRIA ROM MICROPROGRAMADA
  //   00100 = SOMA
  //   01000 = COMPARAÇÃO
  //   00001 = Sub
  //   00010= mult
  //   10000= Divisao
  //   contents of rom_1 (hex, n*v repeats v):
  //   2 15 60 80 0 0 100 14 60 2000 10000 80 0 100 14 260 1400 2000 110000 80 0 100 4 8000 20 8000 8 10000
  //   80 0 100 14 260 800 10000 80 0 100 14 260 21000 2000 110000 80 0 100 14 260 41000 2000 110000 80 0
  //   100 14 260 81000 2000 110000 80 0 100 10000 80
  //   SINAIS DE CONTROLE
endmodule
