// Logisim project 8_cpu com Display de 7 segmentos.circ as structural Verilog: 1 circuit, main circuit main
module main (
  input  CLOCK,
  output [11:0] ACC_OUT
);

  wire main_1_p6, main_1_p7, main_1_p9, main_1_p10, main_1_p11, main_1_p12, main_2_p6, main_2_p7, main_2_p8,
       main_2_p9, main_2_p10, main_2_p11, main_2_p12, n5_ula_1_a_maior_b, n5_ula_1_b_maior_a, n5_ula_1_iguais;
  wire [4:0] uc_1_operacao;
  wire [7:0] n1_pc_1_contador, PC_BUS_out, REM_q, \uc_1_endereço ;
  wire [11:0] n5_ula_1_acc_out, ram_1_data, RDM_q, RI_CLEAR_out, RI_q;
  wire [20:0] uc_1_out_5;

  _1_pc u_1_pc_1 (.PC_TG(uc_1_out_5[0]), .CONTADOR(n1_pc_1_contador));  // open: PC_CLEAR
  assign RI_CLEAR_out = uc_1_out_5[16] ? {12{1'b0}} : 12'bz;  // Controlled_Buffer RI_CLEAR
  assign PC_BUS_out = uc_1_out_5[1] ? n1_pc_1_contador : 8'bz;  // Controlled_Buffer PC_BUS
  assign PC_BUS_out = uc_1_out_5[8] ? \uc_1_endereço  : 8'bz;  // Controlled_Buffer UC_BUS
  Register #(.width(12)) RI (.D(RI_CLEAR_out), .Q(RI_q), .clk(uc_1_out_5[7]));  // open: en, clr
  UC uc_1 (.INPUT(RI_q), .\ENDEREÇO (\uc_1_endereço ), .OPERACAO(uc_1_operacao), .out_5(uc_1_out_5), .clock(CLOCK));
  Clock u_CLOCK ();  // open: out
  Register REM (.D(PC_BUS_out), .Q(REM_q), .clk(uc_1_out_5[2]));  // open: en, clr
  _5_ula u_5_ula_1 (
    .ACC_IN(ACC_OUT), .INPUT(RI_CLEAR_out), .A_MAIOR_B(n5_ula_1_a_maior_b), .IGUAIS(n5_ula_1_iguais),
    .B_MAIOR_A(n5_ula_1_b_maior_a), .ULA_TG(uc_1_out_5[9]), .OPERACAO(uc_1_operacao),
    .ADD_TG(uc_1_out_5[10]), .COMP_TG(uc_1_out_5[11]), .ACC_OUT(n5_ula_1_acc_out), .SUB(uc_1_out_5[17]),
    .DIV(uc_1_out_5[19]), .MULT(uc_1_out_5[18]), .Reset_TG(uc_1_out_5[20]));
  LED A_MAIOR_B (.in(n5_ula_1_a_maior_b));
  LED IGUAIS (.in(n5_ula_1_iguais));
  LED B_MAIOR_A (.in(n5_ula_1_b_maior_a));
  RAM #(.dataWidth(12)) ram_1 (
    .addr(REM_q), .data(ram_1_data), .clk(uc_1_out_5[3]), .ld(uc_1_out_5[4]));  // open: sel, clr
  assign RI_CLEAR_out = uc_1_out_5[12] ? n5_ula_1_acc_out : 12'bz;  // Controlled_Buffer ULA_BUS
  Register #(.width(12)) RDM (.D(ram_1_data), .Q(RDM_q), .clk(uc_1_out_5[5]));  // open: en, clr
  _3_acc u_3_acc_1 (.IN(RI_CLEAR_out), .ACC_TG(uc_1_out_5[13]), .ACC_CLEAR(uc_1_out_5[14]), .ACC_OUT(ACC_OUT));
  _7_Segment_Display u_7_segment_display_1 (
    .g(main_1_p12), .f(main_1_p11), .a(main_1_p6), .b(main_1_p7), .e(main_1_p10), .d(main_1_p9), .c(main_1_p7));  // open: dp
  assign RI_CLEAR_out = uc_1_out_5[6] ? RDM_q : 12'bz;  // Controlled_Buffer RDM_BUS
  _7_Segment_Display u_7_segment_display_2 (
    .g(main_2_p12), .f(main_2_p11), .a(main_2_p6), .b(main_2_p7), .e(main_2_p10), .d(main_2_p9), .c(main_2_p8));  // open: dp
  assign ram_1_data = uc_1_out_5[15] ? ACC_OUT : 12'bz;  // Controlled_Buffer ACC_BUS
  // SEGUNDO_DIGITO_main main_1: pin names not known; wires that end beside it: ACC_OUT[4], ACC_OUT[3], ACC_OUT[2], ACC_OUT[1], ACC_OUT[0], main_1_p6, main_1_p7, main_1_p7, main_1_p9, main_1_p10, main_1_p11, main_1_p12
  // decocificador_comp_resultado_main main_2: pin names not known; wires that end beside it: ACC_OUT[4], ACC_OUT[3], ACC_OUT[2], ACC_OUT[1], ACC_OUT[0], main_2_p6, main_2_p7, main_2_p8, main_2_p9, main_2_p10, main_2_p11, main_2_p12

  // Notes on the sheet:
  //   ARQUITETURA DE COMPUTADORES - CPU TOLEDO v4.0 - AUTOMÁTICA
  //   MEMÓRIA RAM
endmodule
